# Fritzing sketch blink_led (saved by Fritzing 0.9.3b)
breadboards: 1

parts:
  R1 = Resistor [tolerance=±5% resistance=220 package=THT]
  LED1 = LED - 5mm [color="Red (633nm)" package="5 mm [THT]"]
  Part1 = Arduino Uno (Rev3)

nets:
  N1: R1.Pin_0, Part1.A0
  N2: R1.Pin_1, LED1.cathode
  N3: LED1.anode, Part1.GND
